// Logisim project F3.circ as structural Verilog: 3 circuits, main circuit main
module main (
  input  in_1,
  input  in_2,
  input  in_3,
  input  in_4,
  input  in_5,
  input  in_6,
  input  in_7,
  input  in_8,
  input  in_9,
  input  in_10,
  input  in_11,
  input  in_12,
  input  in_13,
  input  in_14,
  input  in_15,
  input  in_16,
  input  in_17,
  input  in_18,
  input  in_19,
  input  in_20,
  input  in_21,
  input  in_22,
  input  in_23,
  input  in_24,
  input  in_25,
  input  in_26,
  input  in_27,
  input  in_28,
  input  in_29,
  input  in_30,
  input  in_31,
  input  in_32,
  input  in_33,
  input  in_34,
  input  in_35,
  input  in_36,
  input  in_37,
  input  in_38,
  input  in_39,
  input  in_40,
  input  in_41,
  input  in_42,
  input  in_43,
  input  in_44,
  input  in_45,
  input  in_46,
  input  in_47,
  input  in_48,
  input  in_49,
  input  in_50,
  input  in_51,
  input  in_52,
  input  in_53,
  input  in_54,
  input  in_55,
  input  in_56,
  input  in_57,
  input  in_58,
  output out_59,
  output out_60,
  output out_61,
  output out_62,
  output out_63,
  output out_64,
  output out_65,
  output out_66,
  output out_67,
  output out_68,
  output out_69,
  output out_70,
  output out_71,
  output out_72,
  output out_73,
  output out_74,
  output out_75,
  output out_76,
  output out_77,
  output out_78,
  output out_79,
  output out_80,
  output out_81,
  output out_82,
  output out_83,
  output out_84,
  output out_85,
  output out_86,
  output out_87,
  output out_88,
  output out_89,
  output out_90,
  output out_91,
  output out_92,
  output out_93,
  output out_94,
  output out_95,
  output out_96,
  output out_97,
  output out_98,
  output out_99,
  output out_100,
  output out_101,
  output out_102,
  output out_103,
  output out_104,
  output out_105,
  output out_106
);

  wire AND2_out, and_1_out, and_2_out, and_3_out, and_4_out, and_5_out, and_6_out, and_7_out, and_8_out,
       and_9_out, and_10_out, and_11_out, and_12_out, and_13_out, and_14_out, and_15_out, and_16_out,
       and_17_out, and_18_out, and_19_out, and_20_out, and_21_out, and_22_out, and_23_out, and_24_out,
       and_25_out, and_26_out, and_27_out, and_28_out, and_29_out, and_30_out, and_31_out, and_32_out,
       and_33_out, and_34_out, and_35_out, and_36_out, and_37_out, and_38_out, and_39_out, and_40_out,
       and_41_out, and_42_out, and_43_out, and_44_out, and_45_out, and_46_out, and_47_out, and_48_out,
       and_49_out, and_54_out, and_55_out, and_56_out, and_57_out, and_58_out, and_59_out, and_60_out,
       and_61_out, and_62_out, and_63_out, and_64_out, and_65_out, and_66_out, and_67_out, and_68_out,
       and_69_out, and_70_out, and_71_out, and_72_out, and_73_out, and_74_out, and_75_out, and_76_out,
       and_77_out, and_78_out, and_79_out, and_80_out, and_81_out, and_82_out, and_83_out, and_84_out,
       and_85_out, and_86_out, and_87_out, and_88_out, and_89_out, and_90_out, and_91_out, and_92_out,
       and_93_out, and_94_out, and_95_out, and_96_out, and_97_out, and_98_out, and_99_out, and_100_out,
       and_101_out, and_102_out, and_103_out, and_104_out, and_105_out, and_106_out, and_107_out,
       and_108_out, and_109_out, and_110_out, and_111_out, button_1_out, clock_1_out, d_ff_1_qn,
       decoder_1_out0, decoder_1_out1, decoder_1_out2, decoder_1_out3, decoder_1_out4, decoder_1_out5,
       decoder_1_out6, decoder_1_out7, decoder_1_out8, decoder_1_out9, dipswitch_1_p1, dipswitch_2_p1,
       dipswitch_2_p2, dipswitch_2_p3, dipswitch_2_p4, dipswitch_3_p1, dipswitch_3_p2, dipswitch_3_p3,
       dipswitch_3_p4, dipswitch_4_p1, dipswitch_4_p2, dipswitch_4_p3, dipswitch_4_p4, dipswitch_5_p1,
       dipswitch_5_p2, dipswitch_5_p3, dipswitch_5_p4, dipswitch_5_p5, dipswitch_5_p6, dipswitch_5_p8,
       dipswitch_5_p9, dipswitch_5_p10, dipswitch_5_p11, dipswitch_5_p12, dipswitch_6_p1, dipswitch_10_p1,
       dipswitch_10_p2, dipswitch_10_p3, dipswitch_11_p1, multiplexer_2_out, multiplexer_3_out, nand_1_out,
       nand_2_out, nand_3_out, nand_4_out, nand_6_out, nor_5_out, nor_6_out, nor_7_out, nor_8_out, nor_9_out,
       nor_10_out, nor_11_out, nor_12_out, nor_13_out, nor_15_out, nor_17_out, nor_19_out, nor_21_out,
       nor_22_out, nor_23_out, nor_24_out, nor_25_out, nor_26_out, nor_27_out, nor_28_out, nor_29_out,
       nor_31_out, nor_33_out, nor_35_out, not_1_out, not_2_out, not_3_out, not_4_out, not_5_out, not_6_out,
       not_7_out, not_10_out, not_11_out, not_12_out, not_13_out, not_14_out, not_15_out, not_16_out,
       not_17_out, not_18_out, not_19_out, not_20_out, not_21_out, not_22_out, not_23_out, not_24_out,
       not_25_out, not_26_out, not_27_out, not_28_out, not_29_out, not_30_out, not_31_out, not_32_out,
       not_33_out, not_34_out, not_35_out, not_36_out, not_37_out, or_2_out, or_3_out, or_4_out, or_6_out,
       or_8_out, or_16_out, or_17_out, or_18_out, or_20_out, or_22_out, or_24_out, or_27_out, or_28_out,
       or_29_out, or_30_out, or_32_out, or_33_out, or_34_out, or_35_out, or_36_out, or_37_out, or_38_out,
       or_39_out, or_40_out, or_41_out, or_42_out, or_43_out, or_44_out, or_45_out, or_46_out, or_47_out,
       or_48_out, or_49_out, or_50_out, or_51_out, or_52_out, or_53_out, or_54_out, or_55_out, or_56_out,
       or_57_out, or_58_out, xnor_1_out, xnor_2_out, xnor_3_out, xnor_4_out, xor_1_out, xor_2_out, xor_3_out,
       xor_4_out, xor_5_out, xor_7_out, xor_14_out, xor_15_out, xor_16_out, xor_17_out, xor_20_out,
       xor_21_out, xor_22_out, xor_23_out, xor_25_out, xor_26_out, xor_27_out, xor_29_out, xor_32_out,
       xor_33_out, xor_34_out, xor_35_out, xor_36_out, xor_37_out, xor_40_out, xor_41_out, xor_42_out,
       xor_43_out, xor_44_out, xor_46_out, xor_47_out, xor_48_out, xor_49_out, xor_51_out, xor_52_out,
       xor_54_out, xor_55_out, xor_56_out, xor_58_out, xor_59_out, xor_61_out, xor_62_out, xor_63_out;
  wire [2:0] undriven_2, undriven_3, undriven_4, undriven_5;
  wire [3:0] decoder_2_out0, or_7_out, undriven;
  wire [5:0] decoder_1_out10;

  // DipSwitch dipswitch_1: pin names not known; wires that end beside it: dipswitch_1_p1
  // DipSwitch dipswitch_2: pin names not known; wires that end beside it: dipswitch_2_p1, dipswitch_2_p2, dipswitch_2_p3, dipswitch_2_p4, dipswitch_2_p4
  // DipSwitch dipswitch_3: pin names not known; wires that end beside it: dipswitch_3_p1, dipswitch_3_p2, dipswitch_3_p3, dipswitch_3_p4
  Button button_1 (.out(button_1_out));
  not not_1 (not_1_out, in_2);
  not not_2 (not_2_out, in_1);
  not not_3 (not_3_out, in_3);
  not not_4 (not_4_out, in_7);
  not not_5 (not_5_out, in_6);
  not not_6 (not_6_out, in_9);
  not not_7 (not_7_out, in_8);
  // DipSwitch dipswitch_4: pin names not known; wires that end beside it: dipswitch_4_p1, dipswitch_4_p2, dipswitch_4_p3, dipswitch_4_p4
  // DipSwitch dipswitch_5: pin names not known; wires that end beside it: dipswitch_5_p1, dipswitch_5_p2, dipswitch_5_p3, dipswitch_5_p4, dipswitch_5_p5, dipswitch_5_p6, dipswitch_4_p4, dipswitch_5_p8, dipswitch_5_p9, dipswitch_5_p10, dipswitch_5_p11, dipswitch_5_p12
  // DipSwitch dipswitch_6: pin names not known; wires that end beside it: dipswitch_6_p1
  // DipSwitch dipswitch_7: pin names not known; wires that end beside it: undriven_4[2]
  LED led_1 (.in(or_2_out));
  buf and_1 (and_1_out, not_3_out);  // AND_Gate
  nand nand_1 (nand_1_out, in_6, not_4_out);
  nand nand_2 (nand_2_out, not_5_out, in_7);
  nand nand_3 (nand_3_out, in_8, not_6_out);
  nand nand_4 (nand_4_out, not_7_out, in_9);
  Decoder #(.select(4)) decoder_1 (
    .out0(decoder_1_out0), .out1(decoder_1_out1), .out2(decoder_1_out2), .out3(decoder_1_out3),
    .out4(decoder_1_out4), .out5(decoder_1_out5), .out6(decoder_1_out6), .out7(decoder_1_out7),
    .out8(decoder_1_out8), .out9(decoder_1_out9), .out10(decoder_1_out10[0]), .out11(decoder_1_out10[1]),
    .out12(decoder_1_out10[2]), .out13(decoder_1_out10[3]), .out14(decoder_1_out10[4]),
    .out15(decoder_1_out10[5]), .sel(undriven));  // open: en
  // DipSwitch dipswitch_8: pin names not known
  // DipSwitch dipswitch_9: pin names not known
  // DipSwitch dipswitch_10: pin names not known; wires that end beside it: dipswitch_10_p1, dipswitch_10_p2, dipswitch_10_p3
  // DipSwitch dipswitch_11: pin names not known; wires that end beside it: dipswitch_11_p1
  LED led_2 (.in(or_4_out));
  and and_2 (and_2_out, in_1, not_1_out);
  and AND2 (AND2_out, not_2_out, in_2);
  D_Flip_Flop d_ff_1 (.D(d_ff_1_qn), .clk(and_1_out), .Q(out_63), .Qn(d_ff_1_qn));  // open: preset, reset
  nand nand_5 (out_65, nand_1_out, nand_2_out);
  nand nand_6 (nand_6_out, nand_3_out, nand_4_out);
  or or_1 (or_7_out[3], dipswitch_5_p5, dipswitch_5_p6, dipswitch_4_p4, dipswitch_5_p8, dipswitch_5_p9, dipswitch_5_p10, dipswitch_5_p11, dipswitch_5_p12);
  Priority_Encoder #(.select(4)) priority_encoder_1 ();  // open: in0, in1, in2, in3, in4, in5, in6, in7, in8, in9, in10, in11, in12, in13, in14, in15, out, gs, en_out, en_in
  and and_3 (and_3_out, in_10, in_11);
  and and_4 (and_4_out, in_12, dipswitch_6_p1);
  not not_8 (dipswitch_6_p1, in_10);
  xnor xnor_1 (xnor_1_out, dipswitch_2_p1, dipswitch_3_p1);
  xnor xnor_2 (xnor_2_out, dipswitch_2_p2, dipswitch_3_p2);
  xnor xnor_3 (xnor_3_out, dipswitch_2_p3, dipswitch_3_p3);
  xnor xnor_4 (xnor_4_out, dipswitch_2_p4, dipswitch_3_p4);
  and and_5 (and_5_out, in_15, in_17);
  and and_6 (and_6_out, in_15, in_16);
  xor xor_1 (xor_1_out, in_15, in_16);
  and and_7 (and_7_out, in_16, in_17);
  and and_8 (and_8_out, in_18, out_71);
  and and_9 (and_9_out, in_18, in_19);
  xor xor_2 (xor_2_out, in_18, in_19);
  and and_10 (and_10_out, in_19, out_71);
  and and_11 (and_11_out, in_20, out_73);
  and and_12 (and_12_out, in_20, in_21);
  xor xor_3 (xor_3_out, in_20, in_21);
  and and_13 (and_13_out, in_21, out_73);
  and and_14 (and_14_out, in_22, out_75);
  and and_15 (and_15_out, in_22, in_23);
  xor xor_4 (xor_4_out, in_22, in_23);
  and and_16 (and_16_out, in_23, out_75);
  and and_17 (and_17_out, or_27_out, xor_14_out);
  and and_18 (and_18_out, in_24, or_27_out);
  or or_2 (or_2_out, and_17_out, and_18_out, and_24_out);
  and and_19 (and_19_out, or_28_out, xor_15_out);
  and and_20 (and_20_out, in_34, or_28_out);
  or or_3 (or_3_out, and_19_out, and_20_out, and_25_out);
  or or_4 (or_4_out, and_21_out, and_22_out, and_30_out);
  or or_5 (out_60, and_2_out, AND2_out);
  // Probe on {in_5, in_4}
  not not_9 (out_66, nand_6_out);
  or or_6 (or_6_out, decoder_1_out0, decoder_1_out2, decoder_1_out3, decoder_1_out5, decoder_1_out6, decoder_1_out7, decoder_1_out8, decoder_1_out9);
  or or_7 (or_7_out[0], dipswitch_4_p1, dipswitch_4_p3, dipswitch_5_p2, dipswitch_5_p4, dipswitch_5_p6, dipswitch_5_p8, dipswitch_5_p10, dipswitch_5_p12);
  Multiplexer #(.select(2), .width(3)) multiplexer_1 (
    .in0(undriven_2), .in1(undriven_3), .in2(undriven_4), .in3(undriven_5), .out({out_70, out_69, out_68}),
    .sel({in_14, in_13}));
  xor xor_5 (xor_5_out, in_24, xor_14_out);
  xor xor_6 (out_79, or_27_out, xor_5_out);
  xor xor_7 (xor_7_out, in_34, xor_15_out);
  xor xor_8 (out_83, or_28_out, xor_7_out);
  not not_10 (not_10_out, out_89);
  not not_11 (not_11_out, not_10_out);
  and and_21 (and_21_out, or_30_out, xor_16_out);
  and and_22 (and_22_out, out_98, or_30_out);
  xor xor_9 (out_103, or_30_out, xor_17_out);
  Decoder #(.select(2)) decoder_2 (
    .out0(decoder_2_out0[0]), .out1(decoder_2_out0[1]), .out2(decoder_2_out0[2]), .out3(decoder_2_out0[3]),
    .sel({in_5, in_4}));  // open: en
  or or_8 (or_8_out, decoder_1_out10[0], decoder_1_out10[1], decoder_1_out10[2], decoder_1_out10[3], decoder_1_out10[4], decoder_1_out10[5]);
  or or_9 (or_7_out[2], dipswitch_5_p1, dipswitch_5_p2, dipswitch_5_p3, dipswitch_5_p4, dipswitch_5_p12, dipswitch_5_p11, dipswitch_5_p10, dipswitch_5_p9);
  // OR_Gate or_10 is placed but not wired
  or or_11 (out_67, and_3_out, and_4_out);
  and and_23 (and_23_out, xnor_1_out, xnor_2_out, xnor_3_out, xnor_4_out);
  or or_12 (out_71, and_5_out, and_6_out, and_7_out);
  xor xor_10 (out_72, xor_1_out, in_17);
  or or_13 (out_73, and_8_out, and_9_out, and_10_out);
  xor xor_11 (out_74, xor_2_out, out_71);
  or or_14 (out_75, and_11_out, and_12_out, and_13_out);
  xor xor_12 (out_76, xor_3_out, out_73);
  LED led_3 (.in(out_77));
  or or_15 (out_77, and_14_out, and_15_out, and_16_out);
  xor xor_13 (out_78, xor_4_out, out_75);
  xor xor_14 (xor_14_out, in_25, in_32);
  and and_24 (and_24_out, xor_14_out, in_24);
  xor xor_15 (xor_15_out, in_35, in_42);
  and and_25 (and_25_out, xor_15_out, in_34);
  and and_26 (and_26_out, out_106, in_46);
  and and_27 (and_27_out, out_105, in_46);
  and and_28 (and_28_out, out_104, in_46);
  and and_29 (and_29_out, out_103, in_46);
  xor xor_16 (xor_16_out, in_52, in_56);
  xor xor_17 (xor_17_out, out_98, xor_16_out);
  // Probe on decoder_2_out0
  or or_16 (or_16_out, decoder_1_out0, decoder_1_out1, decoder_1_out2, decoder_1_out3, decoder_1_out4, decoder_1_out7, decoder_1_out8, decoder_1_out9);
  or or_17 (or_17_out, decoder_1_out0, decoder_1_out1, decoder_1_out3, decoder_1_out4, decoder_1_out5, decoder_1_out6, decoder_1_out7, decoder_1_out8, decoder_1_out9);
  or or_18 (or_18_out, decoder_1_out0, decoder_1_out2, decoder_1_out3, decoder_1_out5, decoder_1_out6, decoder_1_out8, decoder_1_out9);
  // OR_Gate or_19 is placed but not wired
  or or_20 (or_20_out, decoder_1_out0, decoder_1_out2, decoder_1_out6, decoder_1_out8);
  // OR_Gate or_21 is placed but not wired
  or or_22 (or_22_out, decoder_1_out0, decoder_1_out4, decoder_1_out5, decoder_1_out6, decoder_1_out7, decoder_1_out8, decoder_1_out9);
  // OR_Gate or_23 is placed but not wired
  or or_24 (or_24_out, decoder_1_out2, decoder_1_out3, decoder_1_out4, decoder_1_out5, decoder_1_out6, decoder_1_out8, decoder_1_out9);
  // OR_Gate or_25 is placed but not wired
  Multiplexer multiplexer_2 (.in0(or_8_out), .out(multiplexer_2_out), .sel(dipswitch_1_p1));  // open: in1
  or or_26 (or_7_out[1], dipswitch_4_p2, dipswitch_4_p3, dipswitch_5_p3, dipswitch_5_p4, dipswitch_4_p4, dipswitch_5_p8, dipswitch_5_p11, dipswitch_5_p12);
  LED led_4 (.in(and_23_out));
  or or_27 (or_27_out, and_31_out, and_32_out, and_47_out);
  or or_28 (or_28_out, and_33_out, and_34_out, and_48_out);
  nor nor_1 (out_87, dipswitch_10_p1, out_88);
  nor nor_2 (out_88, out_87, dipswitch_10_p2);
  not not_12 (not_12_out, and_26_out);
  not not_13 (not_13_out, button_1_out);
  not not_14 (not_14_out, and_27_out);
  not not_15 (not_15_out, button_1_out);
  not not_16 (not_16_out, and_28_out);
  not not_17 (not_17_out, button_1_out);
  not not_18 (not_18_out, and_29_out);
  not not_19 (not_19_out, button_1_out);
  and and_30 (and_30_out, xor_16_out, out_98);
  not not_20 (not_20_out, in_4);
  not not_21 (not_21_out, in_5);
  Multiplexer multiplexer_3 (.in0(or_24_out), .in1(or_29_out), .out(multiplexer_3_out), .sel(dipswitch_1_p1));
  // OR_Gate or_29 has open pins: out=or_29_out
  Hex_Digit_Display hex_digit_display_1 (.value(or_7_out));  // open: dp
  and and_31 (and_31_out, or_37_out, xor_20_out);
  and and_32 (and_32_out, in_26, or_37_out);
  xor xor_18 (out_80, or_37_out, xor_21_out);
  and and_33 (and_33_out, or_38_out, xor_22_out);
  and and_34 (and_34_out, in_36, or_38_out);
  xor xor_19 (out_84, or_38_out, xor_23_out);
  and and_35 (and_35_out, not_10_out, dipswitch_11_p1);
  and and_36 (and_36_out, dipswitch_11_p1, not_11_out);
  or or_30 (or_30_out, and_45_out, and_46_out, and_49_out);
  _7_Segment_Display u_7_segment_display_1 (
    .g(multiplexer_3_out), .f(or_22_out), .a(or_6_out), .b(or_16_out), .e(or_20_out), .d(or_18_out),
    .c(or_17_out), .dp(multiplexer_2_out));
  // OR_Gate or_31 has open pins: in6=or_29_out, out=open
  xor xor_20 (xor_20_out, in_27, in_32);
  xor xor_21 (xor_21_out, in_26, xor_20_out);
  xor xor_22 (xor_22_out, in_37, in_42);
  xor xor_23 (xor_23_out, in_36, xor_22_out);
  or or_32 (or_32_out, and_36_out, in_44);
  and and_37 (and_37_out, not_12_out, not_13_out);
  and and_38 (and_38_out, not_13_out, and_26_out);
  and and_39 (and_39_out, not_14_out, not_15_out);
  and and_40 (and_40_out, not_15_out, and_27_out);
  and and_41 (and_41_out, not_16_out, not_17_out);
  and and_42 (and_42_out, not_17_out, and_28_out);
  and and_43 (and_43_out, not_18_out, not_19_out);
  and and_44 (and_44_out, not_19_out, and_29_out);
  and and_45 (and_45_out, or_39_out, xor_25_out);
  and and_46 (and_46_out, out_96, or_39_out);
  xor xor_24 (out_104, or_39_out, xor_26_out);
  Decoder2to4 decoder2to4_1 (.in_1(in_4), .in_2(in_5));  // open: out_3, out_4, out_5, out_6
  Hex_Digit_Display hex_digit_display_2 (.value({out_78, out_76, out_74, out_72}));  // open: dp
  and and_47 (and_47_out, xor_20_out, in_26);
  and and_48 (and_48_out, xor_22_out, in_36);
  or or_33 (or_33_out, and_38_out, in_48);
  or or_34 (or_34_out, and_40_out, in_48);
  or or_35 (or_35_out, and_42_out, in_48);
  or or_36 (or_36_out, and_44_out, in_48);
  xor xor_25 (xor_25_out, in_53, in_56);
  xor xor_26 (xor_26_out, out_96, xor_25_out);
  and and_49 (and_49_out, xor_25_out, out_96);
  and and_50 (out_59, not_20_out, not_21_out);
  and and_51 (out_61, in_4, not_21_out);
  and and_52 (out_62, not_20_out, in_5);
  and and_53 (out_64, in_4, in_5);
  and and_54 (and_54_out, or_40_out, xor_32_out);
  and and_55 (and_55_out, in_28, or_40_out);
  or or_37 (or_37_out, and_54_out, and_55_out, and_60_out);
  and and_56 (and_56_out, or_41_out, xor_33_out);
  and and_57 (and_57_out, in_38, or_41_out);
  or or_38 (or_38_out, and_56_out, and_57_out, and_61_out);
  nor nor_3 (out_89, and_35_out, out_90);
  nor nor_4 (out_90, out_89, or_32_out);
  or or_39 (or_39_out, and_58_out, and_59_out, and_62_out);
  xor xor_27 (xor_27_out, in_28, xor_32_out);
  xor xor_28 (out_81, or_40_out, xor_27_out);
  xor xor_29 (xor_29_out, in_38, xor_33_out);
  xor xor_30 (out_85, or_41_out, xor_29_out);
  nor nor_5 (nor_5_out, and_37_out, nor_6_out);
  nor nor_6 (nor_6_out, nor_5_out, or_33_out);
  nor nor_7 (nor_7_out, and_39_out, nor_8_out);
  nor nor_8 (nor_8_out, nor_7_out, or_34_out);
  nor nor_9 (nor_9_out, and_41_out, nor_10_out);
  nor nor_10 (nor_10_out, nor_9_out, or_35_out);
  nor nor_11 (nor_11_out, and_43_out, nor_12_out);
  nor nor_12 (nor_12_out, nor_11_out, or_36_out);
  and and_58 (and_58_out, or_42_out, xor_34_out);
  and and_59 (and_59_out, out_94, or_42_out);
  xor xor_31 (out_105, or_42_out, xor_35_out);
  xor xor_32 (xor_32_out, in_29, in_32);
  and and_60 (and_60_out, xor_32_out, in_28);
  xor xor_33 (xor_33_out, in_39, in_42);
  and and_61 (and_61_out, xor_33_out, in_38);
  xor xor_34 (xor_34_out, in_54, in_56);
  xor xor_35 (xor_35_out, out_94, xor_34_out);
  or or_40 (or_40_out, and_63_out, and_64_out, and_77_out);
  xor xor_36 (xor_36_out, or_2_out, in_32);
  _7_Segment_Display u_7_segment_display_2 (.g(xor_36_out));  // open: f, a, b, e, d, c, dp
  or or_41 (or_41_out, and_65_out, and_66_out, and_78_out);
  xor xor_37 (xor_37_out, or_3_out, in_42);
  _7_Segment_Display u_7_segment_display_3 (.g(xor_37_out));  // open: f, a, b, e, d, c, dp
  not not_22 (not_22_out, nor_6_out);
  not not_23 (not_23_out, nor_8_out);
  not not_24 (not_24_out, nor_10_out);
  not not_25 (not_25_out, nor_12_out);
  and and_62 (and_62_out, xor_34_out, out_94);
  and and_63 (and_63_out, xor_46_out, xor_41_out);
  and and_64 (and_64_out, in_30, xor_46_out);
  xor xor_38 (out_82, xor_46_out, xor_42_out);
  Hex_Digit_Display hex_digit_display_3 (.value({out_79, out_80, out_81, out_82}));  // open: dp
  and and_65 (and_65_out, in_43, xor_43_out);
  and and_66 (and_66_out, in_40, in_43);
  xor xor_39 (out_86, in_43, xor_44_out);
  Hex_Digit_Display hex_digit_display_4 (.value({out_83, out_84, out_85, out_86}));  // open: dp
  and and_67 (and_67_out, not_22_out, button_1_out);
  and and_68 (and_68_out, button_1_out, nor_6_out);
  and and_69 (and_69_out, not_23_out, button_1_out);
  and and_70 (and_70_out, button_1_out, nor_8_out);
  and and_71 (and_71_out, not_24_out, button_1_out);
  and and_72 (and_72_out, button_1_out, nor_10_out);
  and and_73 (and_73_out, not_25_out, button_1_out);
  and and_74 (and_74_out, button_1_out, nor_12_out);
  or or_42 (or_42_out, and_75_out, and_76_out, and_79_out);
  xor xor_40 (xor_40_out, or_4_out, in_56);
  _7_Segment_Display u_7_segment_display_4 (.g(xor_40_out));  // open: f, a, b, e, d, c, dp
  Hex_Digit_Display hex_digit_display_5 (.value({out_103, out_104, out_105, out_106}));  // open: dp
  xor xor_41 (xor_41_out, in_31, in_32);
  xor xor_42 (xor_42_out, in_30, xor_41_out);
  xor xor_43 (xor_43_out, in_41, in_42);
  xor xor_44 (xor_44_out, in_40, xor_43_out);
  or or_43 (or_43_out, and_68_out, in_48);
  or or_44 (or_44_out, and_70_out, in_48);
  or or_45 (or_45_out, and_72_out, in_48);
  or or_46 (or_46_out, and_74_out, in_48);
  and and_75 (and_75_out, xor_49_out, xor_47_out);
  and and_76 (and_76_out, out_92, xor_49_out);
  xor xor_45 (out_106, xor_49_out, xor_48_out);
  and and_77 (and_77_out, xor_41_out, in_30);
  xor xor_46 (xor_46_out, in_32, in_33);
  and and_78 (and_78_out, xor_43_out, in_40);
  xor xor_47 (xor_47_out, in_46, in_56);
  xor xor_48 (xor_48_out, out_92, xor_47_out);
  and and_79 (and_79_out, xor_47_out, out_92);
  nor nor_13 (nor_13_out, and_67_out, out_92);
  nor nor_14 (out_92, nor_13_out, or_43_out);
  nor nor_15 (nor_15_out, and_69_out, out_94);
  nor nor_16 (out_94, nor_15_out, or_44_out);
  nor nor_17 (nor_17_out, and_71_out, out_96);
  nor nor_18 (out_96, nor_17_out, or_45_out);
  nor nor_19 (nor_19_out, and_73_out, out_98);
  nor nor_20 (out_98, nor_19_out, or_46_out);
  xor xor_49 (xor_49_out, in_56, in_58);
  Hex_Digit_Display hex_digit_display_6 (.value({out_98, out_96, out_94, out_92}));  // open: dp
  Clock clock_1 (.out(clock_1_out));
  or or_47 (or_47_out, and_80_out, and_81_out, and_86_out);
  LED led_5 (.in(or_47_out));
  and and_80 (and_80_out, or_48_out, xor_51_out);
  and and_81 (and_81_out, out_97, or_48_out);
  xor xor_50 (out_99, or_48_out, xor_52_out);
  and and_82 (and_82_out, out_102, in_45);
  and and_83 (and_83_out, out_101, in_45);
  and and_84 (and_84_out, out_100, in_45);
  and and_85 (and_85_out, out_99, in_45);
  xor xor_51 (xor_51_out, in_49, in_55);
  xor xor_52 (xor_52_out, out_97, xor_51_out);
  not not_26 (not_26_out, and_82_out);
  not not_27 (not_27_out, clock_1_out);
  not not_28 (not_28_out, and_83_out);
  not not_29 (not_29_out, clock_1_out);
  not not_30 (not_30_out, and_84_out);
  not not_31 (not_31_out, clock_1_out);
  not not_32 (not_32_out, and_85_out);
  not not_33 (not_33_out, clock_1_out);
  and and_86 (and_86_out, xor_51_out, out_97);
  or or_48 (or_48_out, and_95_out, and_96_out, and_97_out);
  and and_87 (and_87_out, not_26_out, not_27_out);
  and and_88 (and_88_out, not_27_out, and_82_out);
  and and_89 (and_89_out, not_28_out, not_29_out);
  and and_90 (and_90_out, not_29_out, and_83_out);
  and and_91 (and_91_out, not_30_out, not_31_out);
  and and_92 (and_92_out, not_31_out, and_84_out);
  and and_93 (and_93_out, not_32_out, not_33_out);
  and and_94 (and_94_out, not_33_out, and_85_out);
  and and_95 (and_95_out, or_53_out, xor_54_out);
  and and_96 (and_96_out, out_95, or_53_out);
  xor xor_53 (out_100, or_53_out, xor_55_out);
  or or_49 (or_49_out, and_88_out, in_47);
  or or_50 (or_50_out, and_90_out, in_47);
  or or_51 (or_51_out, and_92_out, in_47);
  or or_52 (or_52_out, and_94_out, in_47);
  xor xor_54 (xor_54_out, in_50, in_55);
  xor xor_55 (xor_55_out, out_95, xor_54_out);
  and and_97 (and_97_out, xor_54_out, out_95);
  nor nor_21 (nor_21_out, and_87_out, nor_22_out);
  nor nor_22 (nor_22_out, nor_21_out, or_49_out);
  nor nor_23 (nor_23_out, and_89_out, nor_24_out);
  nor nor_24 (nor_24_out, nor_23_out, or_50_out);
  nor nor_25 (nor_25_out, and_91_out, nor_26_out);
  nor nor_26 (nor_26_out, nor_25_out, or_51_out);
  nor nor_27 (nor_27_out, and_93_out, nor_28_out);
  nor nor_28 (nor_28_out, nor_27_out, or_52_out);
  and and_98 (and_98_out, or_54_out, xor_58_out);
  and and_99 (and_99_out, out_93, or_54_out);
  or or_53 (or_53_out, and_98_out, and_99_out, and_100_out);
  xor xor_56 (xor_56_out, out_93, xor_58_out);
  xor xor_57 (out_101, or_54_out, xor_56_out);
  not not_34 (not_34_out, nor_22_out);
  not not_35 (not_35_out, nor_24_out);
  not not_36 (not_36_out, nor_26_out);
  not not_37 (not_37_out, nor_28_out);
  xor xor_58 (xor_58_out, in_51, in_55);
  and and_100 (and_100_out, xor_58_out, out_93);
  and and_101 (and_101_out, not_34_out, clock_1_out);
  and and_102 (and_102_out, clock_1_out, nor_22_out);
  and and_103 (and_103_out, not_35_out, clock_1_out);
  and and_104 (and_104_out, clock_1_out, nor_24_out);
  and and_105 (and_105_out, not_36_out, clock_1_out);
  and and_106 (and_106_out, clock_1_out, nor_26_out);
  and and_107 (and_107_out, not_37_out, clock_1_out);
  and and_108 (and_108_out, clock_1_out, nor_28_out);
  or or_54 (or_54_out, and_109_out, and_110_out, and_111_out);
  xor xor_59 (xor_59_out, or_47_out, in_55);
  _7_Segment_Display u_7_segment_display_5 (.g(xor_59_out));  // open: f, a, b, e, d, c, dp
  Hex_Digit_Display hex_digit_display_7 (.value({out_99, out_100, out_101, out_102}));  // open: dp
  and and_109 (and_109_out, xor_63_out, xor_61_out);
  and and_110 (and_110_out, out_91, xor_63_out);
  xor xor_60 (out_102, xor_63_out, xor_62_out);
  or or_55 (or_55_out, and_102_out, in_47);
  or or_56 (or_56_out, and_104_out, in_47);
  or or_57 (or_57_out, and_106_out, in_47);
  or or_58 (or_58_out, and_108_out, in_47);
  xor xor_61 (xor_61_out, in_45, in_55);
  xor xor_62 (xor_62_out, out_91, xor_61_out);
  and and_111 (and_111_out, xor_61_out, out_91);
  nor nor_29 (nor_29_out, and_101_out, out_91);
  nor nor_30 (out_91, nor_29_out, or_55_out);
  nor nor_31 (nor_31_out, and_103_out, out_93);
  nor nor_32 (out_93, nor_31_out, or_56_out);
  nor nor_33 (nor_33_out, and_105_out, out_95);
  nor nor_34 (out_95, nor_33_out, or_57_out);
  nor nor_35 (nor_35_out, and_107_out, out_97);
  nor nor_36 (out_97, nor_35_out, or_58_out);
  xor xor_63 (xor_63_out, in_55, in_57);
  Hex_Digit_Display hex_digit_display_8 (.value({out_97, out_95, out_93, out_91}));  // open: dp
endmodule

module Decoder2to4 (
  input  in_1,
  input  in_2,
  output out_3,
  output out_4,
  output out_5,
  output out_6
);

  wire not_1_out, not_2_out;

  not not_1 (not_1_out, in_1);
  not not_2 (not_2_out, in_2);
  and and_1 (out_3, not_1_out, not_2_out);
  and and_2 (out_4, in_1, not_2_out);
  and and_3 (out_5, not_1_out, in_2);
  and and_4 (out_6, in_1, in_2);
endmodule

module ClockDesign (
  input  [7:0] in_1,
  input  [7:0] in_2,
  input  [7:0] in_3,
  input  [7:0] in_4,
  input  [7:0] in_5,
  input  in_6,
  input  [7:0] in_7,
  input  [7:0] in_8,
  input  [7:0] in_9,
  input  in_10,
  input  [7:0] in_11,
  input  [7:0] in_12,
  input  [7:0] in_13,
  input  in_14,
  input  [7:0] in_15,
  input  [7:0] in_16,
  input  [7:0] in_17,
  input  in_18,
  input  in_19,
  input  [7:0] in_20,
  output [7:0] out_21
);

  wire button_1_out, button_2_out, clock_1_out, clock_2_out, comparator_1_eq, comparator_2_eq,
       comparator_3_eq, comparator_4_eq, comparator_5_eq;
  wire [3:0] bitselector_1_out, bitselector_2_out, bitselector_3_out, bitselector_4_out;
  wire [7:0] adder_1_out, adder_2_out, adder_3_out, adder_4_out, adder_6_out, multiplexer_1_out,
       multiplexer_2_out, multiplexer_3_out, multiplexer_4_out, multiplexer_5_out, multiplexer_6_out,
       register_1_q, register_2_q, register_3_q, register_4_q, register_5_q, register_6_q;

  Button button_1 (.out(button_1_out));
  Clock clock_1 (.out(clock_1_out));
  Clock clock_2 (.out(clock_2_out));
  Comparator comparator_1 (.a(adder_1_out), .b(in_5), .eq(comparator_1_eq));  // open: gt, lt
  Comparator comparator_2 (.a(adder_2_out), .b(in_8), .eq(comparator_2_eq));  // open: gt, lt
  Comparator comparator_3 (.a(adder_3_out), .b(in_12), .eq(comparator_3_eq));  // open: gt, lt
  Comparator comparator_4 (.a(adder_4_out), .b(in_16), .eq(comparator_4_eq));  // open: gt, lt
  Button button_2 (.out(button_2_out));
  Register register_1 (.D(multiplexer_1_out), .en(in_6), .clk(clock_2_out), .Q(register_1_q), .clr(button_1_out));
  Multiplexer #(.width(8)) multiplexer_1 (
    .in0(adder_1_out), .in1(in_4), .out(multiplexer_1_out), .sel(comparator_1_eq));
  Register register_2 (.D(multiplexer_2_out), .en(in_10), .clk(clock_2_out), .Q(register_2_q), .clr(button_1_out));
  Multiplexer #(.width(8)) multiplexer_2 (
    .in0(adder_2_out), .in1(in_9), .out(multiplexer_2_out), .sel(comparator_2_eq));
  Register register_3 (.D(multiplexer_3_out), .en(in_14), .clk(clock_2_out), .Q(register_3_q), .clr(button_1_out));
  Multiplexer #(.width(8)) multiplexer_3 (
    .in0(adder_3_out), .in1(in_13), .out(multiplexer_3_out), .sel(comparator_3_eq));
  Register register_4 (.D(multiplexer_4_out), .en(in_19), .clk(clock_2_out), .Q(register_4_q), .clr(button_1_out));
  Multiplexer #(.width(8)) multiplexer_4 (
    .in0(adder_4_out), .in1(in_17), .out(multiplexer_4_out), .sel(comparator_4_eq));
  Register register_5 (.D(out_21), .en(in_6), .clk(clock_1_out), .Q(register_5_q), .clr(button_2_out));
  Register register_6 (.D(adder_6_out), .en(in_6), .clk(clock_1_out), .Q(register_6_q), .clr(button_2_out));
  Adder adder_1 (.a(register_1_q), .b(in_7), .out(adder_1_out));  // open: cin, cout
  Adder adder_2 (.a(register_2_q), .b(in_11), .out(adder_2_out), .cin(comparator_1_eq));  // open: cout
  Adder adder_3 (.a(register_3_q), .b(in_15), .out(adder_3_out), .cin(comparator_2_eq));  // open: cout
  Adder adder_4 (.a(register_4_q), .b(in_20), .out(adder_4_out), .cin(comparator_3_eq));  // open: cout
  Comparator comparator_5 (.a(register_6_q), .b(in_3), .eq(comparator_5_eq));  // open: gt, lt
  Multiplexer #(.width(8)) multiplexer_5 (
    .in0(register_6_q), .in1(in_1), .out(multiplexer_5_out), .sel(comparator_5_eq));
  Multiplexer #(.width(8)) multiplexer_6 (.in0(in_2), .in1(in_1), .out(multiplexer_6_out), .sel(comparator_5_eq));
  BitSelector #(.group(4)) bitselector_1 (.in(register_1_q), .out(bitselector_1_out), .sel(in_18));
  Hex_Digit_Display hex_digit_display_1 (.value(bitselector_4_out));  // open: dp
  BitSelector #(.group(4)) bitselector_2 (.in(register_2_q), .out(bitselector_2_out), .sel(in_18));
  BitSelector #(.group(4)) bitselector_3 (.in(register_3_q), .out(bitselector_3_out), .sel(in_18));
  BitSelector #(.group(4)) bitselector_4 (.in(register_4_q), .out(bitselector_4_out), .sel(in_18));
  Adder adder_5 (.a(register_5_q), .b(multiplexer_5_out), .out(out_21));  // open: cin, cout
  Adder adder_6 (.a(register_6_q), .b(multiplexer_6_out), .out(adder_6_out));  // open: cin, cout
  Hex_Digit_Display hex_digit_display_2 (.value(bitselector_3_out));  // open: dp
  Hex_Digit_Display hex_digit_display_3 (.value(bitselector_2_out));  // open: dp
  Hex_Digit_Display hex_digit_display_4 (.value(bitselector_1_out));  // open: dp
endmodule
