// Logisim project F6.circ as structural Verilog: 5 circuits, main circuit main
module main (
  input  in_1
);

  wire clock_1_out, pc_1_reset;
  wire [2:0] decode_1_funct3;
  wire [4:0] decode_1_rd, decode_1_rs1;
  wire [6:0] decode_1_opcode;
  wire [11:0] decode_1_imm;
  wire [23:0] execute_1_pcres, pc_1_currentpc;
  wire [31:0] pc_1_isa;

  Clock clock_1 (.out(clock_1_out));
  PC pc_1 (
    .Restart(in_1), .Clk(clock_1_out), .newPC(execute_1_pcres), .ISA(pc_1_isa), .Reset(pc_1_reset),
    .currentPC(pc_1_currentpc));
  Decode decode_1 (
    .ISA(pc_1_isa), .Funct3(decode_1_funct3), .imm(decode_1_imm), .Rs1(decode_1_rs1), .Rd(decode_1_rd),
    .Opcode(decode_1_opcode));
  Execute execute_1 (
    .Func3(decode_1_funct3), .imm(decode_1_imm), .Rs1(decode_1_rs1), .Rd(decode_1_rd),
    .Opcode(decode_1_opcode), .Clk(clock_1_out), .PC(pc_1_currentpc), .Reset(pc_1_reset),
    .PCRES(execute_1_pcres));
endmodule

module GPR_USE (
  input  R,
  input  [4:0] RS2,
  input  [4:0] RS1,
  input  clk,
  input  [31:0] wdata,
  input  [3:0] rd,
  input  W,
  input  Reset,
  output [31:0] Output1,
  output [31:0] Output2
);

  wire decoder_1_out1, decoder_1_out2, decoder_1_out3, decoder_1_out4, decoder_1_out5, decoder_1_out6,
       decoder_1_out7, decoder_1_out8, decoder_1_out9, decoder_1_out10, decoder_1_out11, decoder_1_out12,
       decoder_1_out13, decoder_1_out14, decoder_1_out15;
  wire [3:0] bitselector_1_out, bitselector_2_out;
  wire [31:0] bit_extender_1_out, multiplexer_1_out, multiplexer_2_out, register_1_q, register_2_q,
       register_3_q, register_4_q, register_5_q, register_6_q, register_7_q, register_8_q, register_9_q,
       register_10_q, register_11_q, register_12_q, register_13_q, register_14_q, register_15_q,
       register_16_q;

  Decoder #(.select(4)) decoder_1 (
    .out1(decoder_1_out1), .out2(decoder_1_out2), .out3(decoder_1_out3), .out4(decoder_1_out4),
    .out5(decoder_1_out5), .out6(decoder_1_out6), .out7(decoder_1_out7), .out8(decoder_1_out8),
    .out9(decoder_1_out9), .out10(decoder_1_out10), .out11(decoder_1_out11), .out12(decoder_1_out12),
    .out13(decoder_1_out13), .out14(decoder_1_out14), .out15(decoder_1_out15), .sel(rd), .en(W));  // open: out0
  Register #(.width(32)) register_1 (.D({32{1'b0}}), .clk(clk), .Q(register_1_q), .clr(Reset));  // open: en
  Register #(.width(32)) register_2 (.D(wdata), .en(decoder_1_out8), .clk(clk), .Q(register_2_q), .clr(Reset));
  Register #(.width(32)) register_3 (.D(wdata), .en(decoder_1_out1), .clk(clk), .Q(register_3_q), .clr(Reset));
  Register #(.width(32)) register_4 (.D(wdata), .en(decoder_1_out9), .clk(clk), .Q(register_4_q), .clr(Reset));
  Register #(.width(32)) register_5 (.D(wdata), .en(decoder_1_out2), .clk(clk), .Q(register_5_q), .clr(Reset));
  Register #(.width(32)) register_6 (.D(wdata), .en(decoder_1_out10), .clk(clk), .Q(register_6_q), .clr(Reset));
  Register #(.width(32)) register_7 (.D(wdata), .en(decoder_1_out3), .clk(clk), .Q(register_7_q), .clr(Reset));
  Register #(.width(32)) register_8 (.D(wdata), .en(decoder_1_out11), .clk(clk), .Q(register_8_q), .clr(Reset));
  Register #(.width(32)) register_9 (.D(wdata), .en(decoder_1_out4), .clk(clk), .Q(register_9_q), .clr(Reset));
  Register #(.width(32)) register_10 (.D(wdata), .en(decoder_1_out12), .clk(clk), .Q(register_10_q), .clr(Reset));
  Register #(.width(32)) register_11 (.D(wdata), .en(decoder_1_out5), .clk(clk), .Q(register_11_q), .clr(Reset));
  Register #(.width(32)) register_12 (.D(wdata), .en(decoder_1_out13), .clk(clk), .Q(register_12_q), .clr(Reset));
  Register #(.width(32)) register_13 (.D(wdata), .en(decoder_1_out6), .clk(clk), .Q(register_13_q), .clr(Reset));
  Register #(.width(32)) register_14 (.D(wdata), .en(decoder_1_out14), .clk(clk), .Q(register_14_q), .clr(Reset));
  BitSelector #(.group(4), .width(5)) bitselector_1 (.in(RS2), .out(bitselector_1_out), .sel(1'b0));
  BitSelector #(.group(4), .width(5)) bitselector_2 (.in(RS1), .out(bitselector_2_out), .sel(1'b0));
  Register #(.width(32)) register_15 (.D(wdata), .en(decoder_1_out7), .clk(clk), .Q(register_15_q), .clr(Reset));
  Register #(.width(32)) register_16 (.D(wdata), .en(decoder_1_out15), .clk(clk), .Q(register_16_q), .clr(Reset));
  Multiplexer #(.select(4), .width(32)) multiplexer_1 (
    .in0(register_1_q), .in1(register_3_q), .in2(register_5_q), .in3(register_7_q), .in4(register_9_q),
    .in5(register_11_q), .in6(register_13_q), .in7(register_15_q), .in8(register_2_q), .in9(register_4_q),
    .in10(register_6_q), .in11(register_8_q), .in12(register_10_q), .in13(register_12_q),
    .in14(register_14_q), .in15(register_16_q), .out(multiplexer_1_out), .sel(bitselector_2_out));
  Multiplexer #(.select(4), .width(32)) multiplexer_2 (
    .in0(register_1_q), .in1(register_3_q), .in2(register_5_q), .in3(register_7_q), .in4(register_9_q),
    .in5(register_11_q), .in6(register_13_q), .in7(register_15_q), .in8(register_2_q), .in9(register_4_q),
    .in10(register_6_q), .in11(register_8_q), .in12(register_10_q), .in13(register_12_q),
    .in14(register_14_q), .in15(register_16_q), .out(multiplexer_2_out), .sel(bitselector_1_out));
  assign bit_extender_1_out = {{31{R}}, R};  // Bit_Extender bit_extender_1
  assign Output1 = bit_extender_1_out & multiplexer_1_out;  // AND_Gate and_1, 32 bits wide
  assign Output2 = bit_extender_1_out & multiplexer_2_out;  // AND_Gate and_2, 32 bits wide
endmodule

module PC (
  input  Restart,
  input  Clk,
  input  [23:0] newPC,
  output [31:0] ISA,
  output Reset,
  output [23:0] currentPC
);

  Register #(.width(24)) register_1 (.D(newPC), .en(1'b1), .clk(Clk), .Q(currentPC), .clr(Restart));
  ROM #(.addrWidth(24), .dataWidth(32)) rom_1 (.addr({2'b00, currentPC[23:2]}), .data(ISA));

  assign Reset = Restart;

  // Notes on the sheet:
  //   contents of rom_1 (hex, n*v repeats v):
  //   413 93137 10113 10b7 dbc08093 80e7 fe012823 fea10923 fea12423 fe914203 fe4109a3 ff012783 f787b3
  //   f787b3 4b6b7 f0068693 fdc10113 d787b3 10000713 f12423 10593 100793 b00513 2112023 12023 12223 e12623
  //   e12823 f10a23 10b7 a8408093 80e7 2012083 2410113 8067 ff410113 112423 10b7 a7c08093 80e7 513 1800093
  //   80e7 812083 513 c10113 8067 852583 feb12823 fe812e23 3437 a0840413 ff014183 3401b3 1c183 ff114203
  //   440233 24203 4181b3 ff214203 440233 24203 4181b3 ff314203 440233 24203 4181b3 3237 a0020213 320233
  //   24203 ffc12403 420233 420233 410233 11b7 85c18193 fe312823 14800193 fe312623 fec22203 20067 1052703
  //   52683 452783 fe810113 e12423 112a23 fed12823 fef12623 13737 c0070713 fe012223 ff314203 fe4102a3
  //   fef14203 fe410223 fe412203 470233 24203 fe4105a3 ff214203 fe4102a3 fee14203 fe410223 fe412203 470233
  //   24203 fe410523 ff114203 fe4102a3 fed14203 fe410223 fe412203 470233 24203 fe4104a3 ff014203 fe4102a3
  //   fec14203 fe410223 fe412203 470233 24203 fe410423 fe812703 c52603 fee12823 fe812e23 3437 a0840413
  //   ff014183 3401b3 1c183 ff114203 440233 24203 4181b3 ff214203 440233 24203 4181b3 ff314203 440233
  //   24203 4181b3 3237 a0020213 320233 24203 ffc12403 420233 420233 410233 66800193 fe312823 28000193
  //   fe312623 fec22203 20067 c68733 10000513 fe812e23 fe912c23 fee12823 50413 ff012483 fe812423 feb14183
  //   3181b3 fe312423 fe914183 3181b3 fe912423 feb14203 420233 fe412423 fe914203 4181b3 3181b3 fe312a23
  //   fe912423 33237 b0020213 feb14183 4181b3 1c183 fe3103a3 fea14183 4181b3 1c183 fe310323 fe914183
  //   4181b3 1c183 fe3102a3 fe814183 4181b3 1c183 fe310223 ff412183 fe412203 440233 120213 fe412423
  //   feb14203 420233 fe412423 fe914203 4181b3 3237 b0820213 320233 ff812483 ffc12403 24203 420233 420233
  //   410233 11b7 86018193 fe312823 38800193 fe312623 fec22203 20067 812703 10000513 812823 e78733
  //   fe812e23 fe912c23 fee12823 50413 ff012483 fe812423 feb14183 3181b3 fe312423 fe914183 3181b3 fe912423
  //   feb14203 420233 fe412423 fe914203 4181b3 3181b3 fe312a23 fe912423 33237 b0020213 feb14183 4181b3
  //   1c183 fe3103a3 fea14183 4181b3 1c183 fe310323 fe914183 4181b3 1c183 fe3102a3 fe814183 4181b3 1c183
  //   fe310223 ff412183 fe412203 440233 120213 fe412423 feb14203 420233 fe412423 fe914203 4181b3 3237
  //   b0820213 320233 ff812483 ffc12403 24203 420233 420233 410233 11b7 86418193 fe312823 49800193
  //   fe312623 fec22203 20067 8*f787b3 d787b3 f787b3 f787b3 20000437 f40433 812783 c60633 c60633 fef12423
  //   feb14183 3181b3 fe312423 fe914183 fff78213 fe412423 feb14203 420233 fe412423 fe914203 4181b3 3237
  //   b1820213 418233 24203 420233 420233 410233 65800193 fe312823 53c00193 fe312623 fec22203 20067 912623
  //   493 40513 c12223 b12023 10b7 de008093 80e7 12583 412603 812783 148493 40040413 c585b3 fef12823
  //   fe912623 fe812e23 fe912c23 4b437 d0040413 ff014183 340233 100193 320023 fec14183 3401b3 18023 24183
  //   ff114483 940233 100493 920023 fed14483 9404b3 48023 24483 9181b3 ff214483 940233 100493 920023
  //   fee14483 9404b3 48023 24483 9181b3 ff314483 940233 100493 920023 fef14483 9404b3 48023 24483 9181b3
  //   3237 a0020213 320233 24203 ff812483 ffc12403 420233 420233 410233 65400193 fe312823 54400193
  //   fe312623 fec22203 20067 c12483 1012403 1412083 1810113 8067 10000713 fec12823 fee12623 fe812e23
  //   fe912c23 4b437 d0040413 ff014183 340233 100193 320023 fec14183 3401b3 18023 24183 ff114483 940233
  //   100493 920023 fed14483 9404b3 48023 24483 9181b3 ff214483 940233 100493 920023 fee14483 9404b3 48023
  //   24483 9181b3 ff314483 940233 100493 920023 fef14483 9404b3 48023 24483 9181b3 3237 a0020213 320233
  //   24203 ff812483 ffc12403 420233 420233 410233 74c00193 fe312823 28000193 fe312623 fec22203 20067
  //   812703 fee12823 fec12623 fe812e23 fe912c23 4b437 d0040413 ff014183 340233 100193 320023 fec14183
  //   3401b3 18023 24183 ff114483 940233 100493 920023 fed14483 9404b3 48023 24483 9181b3 ff214483 940233
  //   100493 920023 fee14483 9404b3 48023 24483 9181b3 ff314483 940233 100493 920023 fef14483 9404b3 48023
  //   24483 9181b3 3237 a0020213 320233 24203 ff812483 ffc12403 420233 420233 410233 11b7 83418193
  //   fe312823 38800193 fe312623 fec22203 20067 1412083 40637 20000537 1810113 1237 de020213 20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
endmodule

module Decode (
  input  [31:0] ISA,
  output [2:0] Funct3,
  output [11:0] imm,
  output [4:0] Rs1,
  output [4:0] Rd,
  output [6:0] Opcode
);


  assign Funct3 = ISA[14:12];
  assign imm = ISA[31:20];
  assign Opcode = ISA[6:0];
  assign Rd = ISA[11:7];
  assign Rs1 = ISA[19:15];
endmodule

module Execute (
  input  [2:0] Func3,
  input  [11:0] imm,
  input  [4:0] Rs1,
  input  [4:0] Rd,
  input  [6:0] Opcode,
  input  Clk,
  input  [23:0] PC,
  input  Reset,
  output [23:0] PCRES
);

  wire and_1_out, and_3_out, and_6_out, comparator_5_eq, comparator_6_eq, comparator_7_eq, comparator_8_eq,
       comparator_9_eq, comparator_10_eq, comparator_11_eq, comparator_12_eq, comparator_13_eq,
       comparator_14_eq, comparator_15_eq, comparator_15_gt, comparator_16_lt, multiplexer_6_out,
       multiplexer_7_out, multiplexer_8_out, multiplexer_9_out, not_1_out, not_2_out, not_3_out, not_4_out,
       not_5_out, or_1_out, or_5_out, or_7_out, or_8_out, or_9_out, R, RRAM, Sel, SelAdd, SelJal, SelLbu,
       SelLu, SelLW, SelSb, W, WRAM;
  wire [1:0] adder_4_out, adder_4_out_2, adder_4_out_3, adder_4_out_4, adder_4_out_5, adder_4_out_6,
       adder_4_out_7, adder_4_out_8, adder_4_out_9, adder_4_out_10, adder_4_out_11, adder_4_out_12,
       adder_4_out_13, adder_4_out_14, adder_4_out_15, adder_4_out_16, bitselector_2_out,
       priority_encoder_1_out;
  wire [3:0] bitselector_1_out;
  wire [7:0] bitselector_3_out, bitselector_4_out, bitselector_5_out, gpr_use_1_output2, gpr_use_1_output2_2,
       gpr_use_1_output2_3, gpr_use_1_output2_4;
  wire [11:0] multiplexer_10_out;
  wire [23:0] bitselector_6_out, newPC;
  wire [31:0] adder_2_out, adder_3_out, AddResult, bit_extender_1_out, bit_extender_2_out,
       bit_extender_3_out, bit_extender_4_out, bit_extender_5_out, divider_1_out, divider_2_out,
       divider_2_rem, gpr_use_1_output1, multiplexer_1_out, multiplexer_2_out, multiplexer_3_out,
       multiplexer_4_out, multiplexer_5_out, multiplexer_11_out, ram_1_dout, RAWRD, shifter_1_out,
       subtractor_1_out;

  assign bit_extender_1_out = {{12{imm[11]}}, {imm, Rs1, Func3}};  // Bit_Extender bit_extender_1
  Shifter #(.width(32)) shifter_1 (.in(bit_extender_1_out), .\dist (5'b01100), .out(shifter_1_out));
  not not_1 (not_1_out, SelLu);
  assign bit_extender_2_out = {{20{imm[11]}}, imm};  // Bit_Extender bit_extender_2
  Adder #(.width(24)) adder_1 (.a(PC), .b(24'h4), .out(newPC));  // open: cin, cout
  Multiplexer #(.width(32)) multiplexer_1 (
    .in0(shifter_1_out), .in1(bit_extender_2_out), .out(multiplexer_1_out), .sel(not_1_out));
  Comparator #(.width(7)) comparator_1 (.a(Opcode), .b(7'b0010011), .eq(Sel));  // open: gt, lt
  Comparator #(.width(7)) comparator_2 (.a(Opcode), .b(7'b1100111), .eq(SelJal));  // open: gt, lt
  Comparator #(.width(7)) comparator_3 (.a(Opcode), .b(7'b0110011), .eq(SelAdd));  // open: gt, lt
  Comparator #(.width(7)) comparator_4 (.a(Opcode), .b(7'b0110111), .eq(SelLu));  // open: gt, lt
  Comparator #(.width(7)) comparator_5 (.a(Opcode), .b(7'b0000011), .eq(comparator_5_eq));  // open: gt, lt
  Comparator #(.width(3)) comparator_6 (.a(Func3), .b(3'b010), .eq(comparator_6_eq));  // open: gt, lt
  Comparator #(.width(3)) comparator_7 (.a(Func3), .b(3'b100), .eq(comparator_7_eq));  // open: gt, lt
  Comparator #(.width(7)) comparator_8 (.a(Opcode), .b(7'b0100011), .eq(comparator_8_eq));  // open: gt, lt
  Comparator #(.width(3)) comparator_9 (.a(Func3), .b(3'b010), .eq(comparator_9_eq));  // open: gt, lt
  Comparator #(.width(3)) comparator_10 (.a(Func3), .b(3'b000), .eq(comparator_10_eq));  // open: gt, lt
  or or_1 (or_1_out, SelAdd, Sel);
  and and_1 (and_1_out, comparator_5_eq, comparator_6_eq);
  and and_2 (SelLbu, comparator_5_eq, comparator_7_eq);
  and and_3 (and_3_out, comparator_8_eq, comparator_9_eq);
  and and_4 (SelSb, comparator_8_eq, comparator_10_eq);
  Multiplexer #(.width(32)) multiplexer_2 (
    .in0(multiplexer_1_out), .in1(AddResult), .out(multiplexer_2_out), .sel(or_1_out));
  assign bit_extender_3_out = {{8{newPC[23]}}, newPC};  // Bit_Extender bit_extender_3
  or or_2 (SelLW, and_1_out, SelLbu);
  BitSelector #(.group(4), .width(5)) bitselector_1 (.in(Rd), .out(bitselector_1_out), .sel(1'b0));
  Multiplexer #(.width(32)) multiplexer_3 (
    .in0(multiplexer_2_out), .in1(bit_extender_3_out), .out(multiplexer_3_out), .sel(SelJal));
  or or_3 (R, SelSb, and_3_out, SelAdd, SelJal, SelLbu, and_1_out, Sel);
  or or_4 (RRAM, and_1_out, SelLbu);
  or or_5 (or_5_out, and_3_out, SelSb);
  Multiplexer #(.width(32)) multiplexer_4 (.in0(multiplexer_3_out), .in1(RAWRD), .out(multiplexer_4_out), .sel(SelLW));
  or or_6 (W, and_1_out, SelLbu, SelAdd, Sel, SelLu, SelJal);
  Comparator #(.width(2)) comparator_11 (.a(bitselector_2_out), .b(2'b00), .eq(comparator_11_eq));  // open: gt, lt
  Comparator #(.width(2)) comparator_12 (.a(bitselector_2_out), .b(2'b01), .eq(comparator_12_eq));  // open: gt, lt
  Comparator #(.width(2)) comparator_13 (.a(bitselector_2_out), .b(2'b10), .eq(comparator_13_eq));  // open: gt, lt
  Comparator #(.width(2)) comparator_14 (.a(bitselector_2_out), .b(2'b11), .eq(comparator_14_eq));  // open: gt, lt
  BitSelector #(.group(2), .width(32)) bitselector_2 (
    .in({adder_4_out_16, adder_4_out_15, adder_4_out_14, adder_4_out_12, adder_4_out_11, adder_4_out_10, adder_4_out_9, adder_4_out_8, adder_4_out_7, adder_4_out_6, adder_4_out_5, adder_4_out_4, adder_4_out_3, adder_4_out_2, adder_4_out, adder_4_out_13}),
    .out(bitselector_2_out), .sel(4'b0000));
  and and_5 (WRAM, or_5_out, not_3_out);
  Multiplexer #(.width(32)) multiplexer_5 (
    .in0({gpr_use_1_output2_4, gpr_use_1_output2_3, gpr_use_1_output2_2, gpr_use_1_output2}),
    .in1(multiplexer_11_out), .out(multiplexer_5_out), .sel(SelSb));
  Multiplexer multiplexer_6 (.in0(comparator_11_eq), .in1(WRAM), .out(multiplexer_6_out), .sel(not_2_out));
  Multiplexer multiplexer_7 (.in0(comparator_12_eq), .in1(WRAM), .out(multiplexer_7_out), .sel(not_2_out));
  Multiplexer multiplexer_8 (.in0(comparator_13_eq), .in1(WRAM), .out(multiplexer_8_out), .sel(not_2_out));
  Multiplexer multiplexer_9 (.in0(comparator_14_eq), .in1(WRAM), .out(multiplexer_9_out), .sel(not_2_out));
  not not_2 (not_2_out, SelSb);
  RAM #(.addrWidth(24), .asyncread("true"), .byteenables("byteEnables"), .dataWidth(32), .\type ("nonvolatile")) ram_1 (
    .addr({adder_4_out_12, adder_4_out_11, adder_4_out_10, adder_4_out_9, adder_4_out_8, adder_4_out_7, adder_4_out_6, adder_4_out_5, adder_4_out_4, adder_4_out_3, adder_4_out_2, adder_4_out}),
    .we(WRAM), .oe(RRAM), .clk(Clk), .din(multiplexer_5_out), .dout(ram_1_dout), .be3(multiplexer_9_out),
    .be2(multiplexer_8_out), .be1(multiplexer_7_out), .be0(multiplexer_6_out));
  Multiplexer #(.width(12)) multiplexer_10 (.in0({imm[11:5], Rd}), .in1(imm), .out(multiplexer_10_out), .sel(SelLW));
  GPR_USE gpr_use_1 (
    .R(R), .RS2(imm[4:0]), .RS1(Rs1), .clk(Clk), .wdata(multiplexer_4_out), .rd(bitselector_1_out), .W(W),
    .Reset(Reset), .Output1(gpr_use_1_output1),
    .Output2({gpr_use_1_output2_4, gpr_use_1_output2_3, gpr_use_1_output2_2, gpr_use_1_output2}));
  Multiplexer #(.select(2), .width(32)) multiplexer_11 (
    .in0({{24{1'b0}}, gpr_use_1_output2}), .in1({{16{1'b0}}, gpr_use_1_output2, {8{1'b0}}}),
    .in2({{8{1'b0}}, gpr_use_1_output2, {16{1'b0}}}), .in3({gpr_use_1_output2, {24{1'b0}}}),
    .out(multiplexer_11_out), .sel(bitselector_2_out));
  Adder #(.width(32)) adder_2 (.a(gpr_use_1_output1), .b(multiplexer_1_out), .out(adder_2_out));  // open: cin, cout
  Adder #(.width(32)) adder_3 (
    .a(gpr_use_1_output1),
    .b({gpr_use_1_output2_4, gpr_use_1_output2_3, gpr_use_1_output2_2, gpr_use_1_output2}), .out(adder_3_out));  // open: cin, cout
  or or_7 (or_7_out, not_4_out, SelAdd);
  Multiplexer #(.width(32)) multiplexer_12 (.in0(adder_2_out), .in1(adder_3_out), .out(AddResult), .sel(or_7_out));
  Adder #(.width(32)) adder_4 (
    .a(gpr_use_1_output1), .b(bit_extender_4_out),
    .out({adder_4_out_16, adder_4_out_15, adder_4_out_14, adder_4_out_12, adder_4_out_11, adder_4_out_10, adder_4_out_9, adder_4_out_8, adder_4_out_7, adder_4_out_6, adder_4_out_5, adder_4_out_4, adder_4_out_3, adder_4_out_2, adder_4_out, adder_4_out_13}));  // open: cin, cout
  assign bit_extender_4_out = {{20{multiplexer_10_out[11]}}, multiplexer_10_out};  // Bit_Extender bit_extender_4
  not not_3 (not_3_out, and_6_out);
  not not_4 (not_4_out, or_8_out);
  or or_8 (or_8_out, SelJal, Sel);
  Priority_Encoder #(.select(2)) priority_encoder_1 (
    .in0(comparator_11_eq), .in1(comparator_12_eq), .in2(comparator_13_eq), .in3(comparator_14_eq),
    .out(priority_encoder_1_out));  // open: gs, en_out, en_in
  not not_5 (not_5_out, SelJal);
  BitSelector #(.group(8), .width(32)) bitselector_3 (
    .in(ram_1_dout), .out(bitselector_3_out), .sel(priority_encoder_1_out));
  Multiplexer #(.width(24)) multiplexer_13 (.in0({AddResult[23:1], 1'b0}), .in1(newPC), .out(PCRES), .sel(not_5_out));
  Subtractor #(.width(32)) subtractor_1 (
    .a({adder_4_out_16, adder_4_out_15, adder_4_out_14, adder_4_out_12, adder_4_out_11, adder_4_out_10, adder_4_out_9, adder_4_out_8, adder_4_out_7, adder_4_out_6, adder_4_out_5, adder_4_out_4, adder_4_out_3, adder_4_out_2, adder_4_out, adder_4_out_13}),
    .b(32'h20000000), .out(subtractor_1_out));  // open: bin, bout
  Comparator #(.width(32)) comparator_15 (
    .a({adder_4_out_16, adder_4_out_15, adder_4_out_14, adder_4_out_12, adder_4_out_11, adder_4_out_10, adder_4_out_9, adder_4_out_8, adder_4_out_7, adder_4_out_6, adder_4_out_5, adder_4_out_4, adder_4_out_3, adder_4_out_2, adder_4_out, adder_4_out_13}),
    .b(32'h20000000), .gt(comparator_15_gt), .eq(comparator_15_eq));  // open: lt
  Comparator #(.width(32)) comparator_16 (
    .a({adder_4_out_16, adder_4_out_15, adder_4_out_14, adder_4_out_12, adder_4_out_11, adder_4_out_10, adder_4_out_9, adder_4_out_8, adder_4_out_7, adder_4_out_6, adder_4_out_5, adder_4_out_4, adder_4_out_3, adder_4_out_2, adder_4_out, adder_4_out_13}),
    .b(32'h20040000), .lt(comparator_16_lt));  // open: gt, eq
  assign bit_extender_5_out = {{24{1'b0}}, bitselector_3_out};  // Bit_Extender bit_extender_5
  Divider #(.width(32)) divider_1 (.a(subtractor_1_out), .b(32'h4), .out(divider_1_out));  // open: upper, rem
  or or_9 (or_9_out, comparator_15_gt, comparator_15_eq);
  Multiplexer #(.width(32)) multiplexer_14 (.in0(ram_1_dout), .in1(bit_extender_5_out), .out(RAWRD), .sel(SelLbu));
  Divider #(.width(32)) divider_2 (
    .a(divider_1_out), .b(32'h100), .out(divider_2_out), .rem(divider_2_rem));  // open: upper
  and and_6 (and_6_out, or_9_out, comparator_16_lt);
  BitSelector #(.group(8), .width(32)) bitselector_4 (.in(divider_2_out), .out(bitselector_4_out), .sel(2'b00));
  BitSelector #(.group(8), .width(32)) bitselector_5 (.in(divider_2_rem), .out(bitselector_5_out), .sel(2'b00));
  BitSelector #(.group(24), .width(32)) bitselector_6 (
    .in({gpr_use_1_output2_4, gpr_use_1_output2_3, gpr_use_1_output2_2, gpr_use_1_output2}),
    .out(bitselector_6_out), .sel(1'b0));
  // RGB_Video #(.cursor("No Cursor"), .height(256), .width(256)) rgb_video_1: pin names not known; wires that end beside it: Reset, Clk, and_6_out, bitselector_5_out, bitselector_4_out, bitselector_6_out
endmodule
